// Logisim project WITCPU.circ as structural Verilog: 8 circuits, main circuit main
module main (
);

  wire Clock_out, not_1_out;

  Clock_part Clock (.out(Clock_out));
  not not_1 (not_1_out, Clock_out);
  T_Flip_Flop Cycle (.clk(not_1_out), .T(1'b1));  // open: Q, Qn, preset, reset, en
  RAM_part #(.dataWidth(16), .bus("separate")) ram_1 ();  // open: addr, din, data, str, sel, clk, ld, clr
endmodule

module ALU (
  input  [15:0] X,
  input  [15:0] Y,
  input  in_3,
  input  [3:0] in_4,
  input  [7:0] in_5,
  output [15:0] out_6
);

  wire [15:0] adder_1_out, and_1_out, divider_1_out, multiplexer_1_out, multiplier_1_out, or_1_out,
       subtractor_1_out, xnor_1_out;

  Adder #(.width(16)) adder_1 (.a(X), .b(Y), .out(adder_1_out));  // open: cin, cout
  Subtractor #(.width(16)) subtractor_1 (.a(X), .b(Y), .out(subtractor_1_out));  // open: bin, bout
  Multiplier #(.width(16)) multiplier_1 (.a(X), .b(Y), .out(multiplier_1_out));  // open: cin, cout
  Divider #(.width(16)) divider_1 (.a(X), .b(Y), .out(divider_1_out));  // open: upper, rem
  assign and_1_out = X & Y;  // AND_Gate and_1, 16 bits wide
  assign or_1_out = X | Y;  // OR_Gate or_1, 16 bits wide
  assign xnor_1_out = ~(X ^ Y);  // XNOR_Gate xnor_1, 16 bits wide
  Multiplexer #(.select(3), .width(16)) multiplexer_1 (
    .in0(adder_1_out), .in1(subtractor_1_out), .in2(multiplier_1_out), .in3(divider_1_out), .in4(and_1_out),
    .in5(or_1_out), .in6(xnor_1_out), .in7({{9{in_5[7]}}, in_5[6:0]}), .out(multiplexer_1_out),
    .sel(in_4[2:0]));  // open: en
  assign out_6 = in_3 ? multiplexer_1_out : 16'bz;  // Controlled_Buffer controlled_buffer_1
endmodule

module Bus_Controller (
  input  clock,
  input  cycle,
  input  [3:0] opcode,
  input  [7:0] imm,
  input  [15:0] \reg ,
  output ALU,
  output reg_write,
  output RAM_read,
  output RAM_write,
  output [7:0] Addr
);

  wire and_1_out, or_1_out;

  and and_1 (and_1_out, ~opcode[1], opcode[2], opcode[3]);  // AND_Gate
  and and_2 (ALU, cycle, ~opcode[3]);  // AND_Gate
  or or_1 (or_1_out, ~opcode[3], and_1_out);  // OR_Gate
  and and_3 (reg_write, clock, cycle, or_1_out);
  or or_2 (RAM_read, ~cycle, and_1_out);  // OR_Gate
  Multiplexer #(.width(8)) multiplexer_1 (.in0(imm), .in1(\reg [7:0]), .out(Addr), .sel(opcode[0]));  // open: en
  and and_4 (RAM_write, clock, cycle, opcode[1], opcode[2], opcode[3]);
  ALU alu_1 ();  // open: X, Y, in_5, in_3, out_6, in_4
endmodule

module Decoder (
  input  [15:0] in_1,
  output [3:0] ry,
  output [3:0] rd,
  output [3:0] rx,
  output [3:0] opcode,
  output [7:0] imm
);


  assign imm = in_1[7:0];
  assign opcode = in_1[15:12];
  assign rd = in_1[7:4];
  assign rx = in_1[11:8];
  assign ry = in_1[3:0];
endmodule

module PC_Controller (
  input  [7:0] pre_pc,
  input  [7:0] imm,
  input  [15:0] RX,
  input  [3:0] opcode,
  output [7:0] out_5
);

  wire and_1_out, comparator_1_eq, comparator_1_gt, comparator_1_lt, multiplexer_1_out, not_1_out;
  wire [7:0] adder_1_out;

  Comparator #(.width(16)) comparator_1 (
    .a(RX), .b({16{1'b0}}), .gt(comparator_1_gt), .eq(comparator_1_eq), .lt(comparator_1_lt));
  Adder adder_1 (.a(pre_pc), .b(8'h1), .out(adder_1_out));  // open: cin, cout
  not not_1 (not_1_out, comparator_1_eq);
  Multiplexer #(.select(2)) multiplexer_1 (
    .in0(comparator_1_eq), .in1(not_1_out), .in2(comparator_1_gt), .in3(comparator_1_lt),
    .out(multiplexer_1_out), .sel(opcode[1:0]));  // open: en
  Multiplexer #(.width(8)) multiplexer_2 (.in0(adder_1_out), .in1(imm), .out(out_5), .sel(and_1_out));  // open: en
  and and_1 (and_1_out, multiplexer_1_out, ~opcode[2], opcode[3]);  // AND_Gate
endmodule

module RAM (
);

  RAM_part #(.dataWidth(16), .bus("separate")) ram_1 ();  // open: addr, din, data, str, sel, clk, ld, clr
endmodule

module Register (
  input  [15:0] DATA,
  input  [3:0] Rx,
  input  in_3,
  input  [3:0] RD,
  input  [3:0] Ry,
  output [15:0] out_6,
  output [15:0] out_7
);

  wire demultiplexer_1_out0, demultiplexer_1_out1, demultiplexer_1_out2, demultiplexer_1_out3,
       demultiplexer_1_out4, demultiplexer_1_out5, demultiplexer_1_out6, demultiplexer_1_out7,
       demultiplexer_1_out8, demultiplexer_1_out9, demultiplexer_1_out10, demultiplexer_1_out11,
       demultiplexer_1_out12, demultiplexer_1_out13, demultiplexer_1_out14, demultiplexer_1_out15;
  wire [15:0] R0_q, R1_q, R2_q, R3_q, R4_q, R5_q, R6_q, R7_q, R8_q, R9_q, Ra_q, Rb_q, Rc_q, Rd_q, Re_q, Rf_q;

  Demultiplexer #(.select(4)) demultiplexer_1 (
    .out0(demultiplexer_1_out0), .out1(demultiplexer_1_out1), .out2(demultiplexer_1_out2),
    .out3(demultiplexer_1_out3), .out4(demultiplexer_1_out4), .out5(demultiplexer_1_out5),
    .out6(demultiplexer_1_out6), .out7(demultiplexer_1_out7), .out8(demultiplexer_1_out8),
    .out9(demultiplexer_1_out9), .out10(demultiplexer_1_out10), .out11(demultiplexer_1_out11),
    .out12(demultiplexer_1_out12), .out13(demultiplexer_1_out13), .out14(demultiplexer_1_out14),
    .out15(demultiplexer_1_out15), .in(in_3), .sel(RD));  // open: en
  Register_part #(.width(16)) R0 (.D({16{1'b0}}), .Q(R0_q), .clk(demultiplexer_1_out0));  // open: en, clr
  Register_part #(.width(16)) R3 (.D(DATA), .Q(R3_q), .clk(demultiplexer_1_out3));  // open: en, clr
  Register_part #(.width(16)) R6 (.D(DATA), .Q(R6_q), .clk(demultiplexer_1_out6));  // open: en, clr
  Register_part #(.width(16)) R9 (.D(DATA), .Q(R9_q), .clk(demultiplexer_1_out9));  // open: en, clr
  Register_part #(.width(16)) Rc (.D(DATA), .Q(Rc_q), .clk(demultiplexer_1_out12));  // open: en, clr
  Register_part #(.width(16)) R1 (.D(DATA), .Q(R1_q), .clk(demultiplexer_1_out1));  // open: en, clr
  Register_part #(.width(16)) R4 (.D(DATA), .Q(R4_q), .clk(demultiplexer_1_out4));  // open: en, clr
  Register_part #(.width(16)) R7 (.D(DATA), .Q(R7_q), .clk(demultiplexer_1_out7));  // open: en, clr
  Register_part #(.width(16)) Ra (.D(DATA), .Q(Ra_q), .clk(demultiplexer_1_out10));  // open: en, clr
  Register_part #(.width(16)) u_Rd (.D(DATA), .Q(Rd_q), .clk(demultiplexer_1_out13));  // open: en, clr
  Register_part #(.width(16)) R2 (.D(DATA), .Q(R2_q), .clk(demultiplexer_1_out2));  // open: en, clr
  Register_part #(.width(16)) R5 (.D(DATA), .Q(R5_q), .clk(demultiplexer_1_out5));  // open: en, clr
  Register_part #(.width(16)) R8 (.D(DATA), .Q(R8_q), .clk(demultiplexer_1_out8));  // open: en, clr
  Register_part #(.width(16)) Rb (.D(DATA), .Q(Rb_q), .clk(demultiplexer_1_out11));  // open: en, clr
  Register_part #(.width(16)) Re (.D(DATA), .Q(Re_q), .clk(demultiplexer_1_out14));  // open: en, clr
  Register_part #(.width(16)) Rf (.D(DATA), .Q(Rf_q), .clk(demultiplexer_1_out15));  // open: en, clr
  Multiplexer #(.select(4), .width(16)) multiplexer_1 (
    .in0(R0_q), .in1(R1_q), .in2(R2_q), .in3(R3_q), .in4(R4_q), .in5(R5_q), .in6(R6_q), .in7(R7_q),
    .in8(R8_q), .in9(R9_q), .in10(Ra_q), .in11(Rb_q), .in12(Rc_q), .in13(Rd_q), .in14(Re_q), .in15(Rf_q),
    .out(out_6), .sel(Rx));  // open: en
  Multiplexer #(.select(4), .width(16)) multiplexer_2 (
    .in0(R0_q), .in1(R1_q), .in2(R2_q), .in3(R3_q), .in4(R4_q), .in5(R5_q), .in6(R6_q), .in7(R8_q),
    .in8(R8_q), .in9(R9_q), .in10(Ra_q), .in11(Rb_q), .in12(Rc_q), .in13(Rd_q), .in14(Re_q), .in15(Rf_q),
    .out(out_7), .sel(Ry));  // open: en
endmodule

module Clock (
  output out_1
);

  wire not_1_out;

  Clock_part Clock (.out(out_1));
  not not_1 (not_1_out, out_1);
  T_Flip_Flop Cycle (.clk(not_1_out), .T(1'b1));  // open: Q, Qn, preset, reset, en
endmodule
