// Logisim project lab4.circ as structural Verilog: 1 circuit, main circuit main
module main (
  input  in_1,
  input  in_2,
  input  in_3,
  input  in_4
);

  wire clock_1_out, d_ff_1_q, undriven, undriven_2, undriven_3;

  Clock clock_1 (.out(clock_1_out));
  D_Flip_Flop d_ff_1 (
    .clk(clock_1_out), .D(in_1), .Q(d_ff_1_q), .preset(undriven), .en(undriven_2), .reset(undriven_3));  // open: Qn
  D_Flip_Flop d_ff_2 (
    .clk(clock_1_out), .D(in_2), .Q(d_ff_1_q), .preset(undriven), .en(undriven_2), .reset(undriven_3));  // open: Qn
  D_Flip_Flop d_ff_3 (
    .clk(clock_1_out), .D(in_3), .Q(d_ff_1_q), .preset(undriven), .en(undriven_2), .reset(undriven_3));  // open: Qn
  D_Flip_Flop d_ff_4 (
    .clk(clock_1_out), .D(in_4), .Q(d_ff_1_q), .preset(undriven), .en(undriven_2), .reset(undriven_3));  // open: Qn
  LED led_1 (.in(d_ff_1_q));

  // Notes on the sheet:
  //    The circuits will be change to green, if all the flip flops are viable.
endmodule
